# Fritzing sketch clock (saved by Fritzing 1.0.1rc)
breadboards: 1

parts:
  DHT1 = DHT22 Humidity and Temperature Sensor
  OLED1 = OLED 128x64 I2C Monochrome Display GND-VDD
  Част1 = Real Time Clock Module - DS1307 RTC Breakout Board
  Част2 = Arduino Nano (Rev3.0)
  R1 = Resistor [tolerance=±5% power=0.25W resistance=4.7k package=THT]

nets:
  VDD: DHT1.VDD, OLED1.VDD, Част1.5V, Част2.5V, R1.Pin_1
  N1: DHT1.DATA, R1.Pin_0
  GND: DHT1.GND, OLED1.GND, Част1.GND, Част2.GND
  N2: OLED1.SCK, Част1.SCL, Част2.A5
  N3: OLED1.SDA, Част1.SDA, Част2.A4

custom parts:
  OLED 128x64 I2C Monochrome Display GND-VDD: OLED 128x64 I2C Monochrome Display. Note: there are two variants of this part, this one is the GND VDD SCK SDA variant. The other is VDD GND SCK SDA. Make sure you select the part that matches your module as using the incorrect part will probably destroy your module! In addition the mounting holes are marked on silkscreen but not by default drilled. If you want drilled mounting holes, copy a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
